// Logisim project MegaDigiFile(1)(1).circ as structural Verilog
module FA0 (
  input  A,
  input  B,
  output S,
  output C
);

  wire nor_1_out;

  nor nor_1 (nor_1_out, A, B);
  and and_1 (C, A, B);
  nor nor_2 (S, nor_1_out, C);

  // Notes on the sheet:
  //   14 Transistors
  //   FA0
  //   2.75
  //   1.75
  //   Vishwa Kumaravel
endmodule

module FA1 (
  input  A,
  input  B,
  output S,
  output C
);

  wire nand_1_out;

  or or_1 (C, A, B);
  nand nand_1 (nand_1_out, A, B);
  nand nand_2 (S, C, nand_1_out);

  // Notes on the sheet:
  //   FA1
  //   14 Transistors
  //   Vishwa Kumaravel
  //   2.75
  //   1.75
endmodule

module FAopt1 (
  input  A,
  input  B,
  input  Cin,
  output S,
  output Cout
);

  wire nand_1_out, nand_2_out, nor_1_out, nor_2_out, nor_3_out, not_1_out, not_2_out;

  nor nor_1 (nor_1_out, A, B);
  nand nand_1 (nand_1_out, A, B);
  nor nor_2 (nor_2_out, nor_1_out, not_1_out);
  not not_1 (not_1_out, nand_1_out);
  nor nor_3 (nor_3_out, nor_2_out, Cin);
  nand nand_2 (nand_2_out, nor_2_out, Cin);
  not not_2 (not_2_out, nand_2_out);
  nand nand_3 (Cout, nand_2_out, nand_1_out);
  nor nor_4 (S, nor_3_out, not_2_out);

  // Notes on the sheet:
  //   Vishwa Kumaravel
  //   B6
  //   32 Transistors
  //   FAopt 1
  //   if Cin < 2.75: 5.5
  //   Else: Cin + 2.75
  //   if Cin < 2.75: 4.75
  //   Else: Cin + 2
endmodule

module FAopt2 (
  input  A,
  input  B,
  input  Cin,
  output S,
  output Cout
);

  wire and_1_out, nand_1_out, nand_2_out, nand_3_out, nor_1_out, nor_2_out, nor_3_out, not_1_out;

  nor nor_1 (nor_1_out, A, B);
  nand nand_1 (nand_1_out, A, B);
  not not_1 (not_1_out, nand_1_out);
  nor nor_2 (nor_2_out, nor_1_out, not_1_out);
  nand nand_2 (nand_2_out, B, Cin);
  nand nand_3 (nand_3_out, Cin, A);
  nor nor_3 (nor_3_out, nor_2_out, Cin);
  and and_1 (and_1_out, nor_2_out, Cin);
  nor nor_4 (S, nor_3_out, and_1_out);
  nand nand_4 (Cout, nand_1_out, nand_2_out, nand_3_out);

  // Notes on the sheet:
  //   B6
  //   Vishwa Kumaravel
  //   Transistors: 42
  //   FAopt 2
  //   if Cin < 2.75: 5.5
  //   Else: Cin + 2.75
  //   Cin + 2.25
endmodule

module FourBitAdder0 (
  input  [3:0] A,
  input  [3:0] B,
  input  cin,
  output [3:0] S,
  output cout
);

  wire faopt1_2_cout, faopt2_1_cout, faopt2_2_cout;

  FAopt1 faopt1_1 (.B(B[3]), .Cin(faopt1_2_cout), .A(A[3]), .S(S[3]), .Cout(cout));
  FAopt1 faopt1_2 (.B(B[2]), .Cin(faopt2_1_cout), .A(A[2]), .S(S[2]), .Cout(faopt1_2_cout));
  FAopt2 faopt2_1 (.B(B[1]), .Cin(faopt2_2_cout), .A(A[1]), .S(S[1]), .Cout(faopt2_1_cout));
  FAopt2 faopt2_2 (.B(B[0]), .Cin(cin), .A(A[0]), .S(S[0]), .Cout(faopt2_2_cout));

  // Notes on the sheet:
  //   8
  //   8.75
  //   6
  //   8.75
  //   4
  //   6.75
  //   5.5
  //   1.75
  //   8
  //   B6
  //   2.75
  //   4 Bit Ripple Adder
  //   Vishwa Kumaravel
  //   #120 Transistors
endmodule

module FourBitAdder1 (
  input  [3:0] A,
  input  [3:0] B,
  output [3:0] S,
  output cout
);

  wire fa1_1_c, faopt1_2_cout, faopt2_1_cout;

  FAopt1 faopt1_1 (.B(B[3]), .Cin(faopt1_2_cout), .A(A[3]), .S(S[3]), .Cout(cout));
  FAopt1 faopt1_2 (.B(B[2]), .Cin(faopt2_1_cout), .A(A[2]), .S(S[2]), .Cout(faopt1_2_cout));
  FAopt2 faopt2_1 (.B(B[1]), .Cin(fa1_1_c), .A(A[1]), .S(S[1]), .Cout(faopt2_1_cout));
  FA1 fa1_1 (.B(B[0]), .A(A[0]), .S(S[0]), .C(fa1_1_c));

  // Notes on the sheet:
  //   8
  //   8.75
  //   6
  //   8.75
  //   4
  //   6.75
  //   5.5
  //   1.75
  //   8
  //   B6
  //   2.75
  //   4 Bit Ripple Adder
  //   Vishwa Kumaravel
  //   #120 Transistors
endmodule

module EightBitRipple (
  input  [7:0] A,
  input  [7:0] B,
  output [7:0] S,
  output cout
);

  wire fa0_1_c, faopt1_2_cout, faopt1_3_cout, faopt1_4_cout, faopt1_5_cout, faopt1_6_cout, faopt2_1_cout;

  FAopt1 faopt1_1 (.B(B[7]), .Cin(faopt1_2_cout), .A(A[7]), .S(S[7]), .Cout(cout));
  FAopt1 faopt1_2 (.B(B[6]), .Cin(faopt1_3_cout), .A(A[6]), .S(S[6]), .Cout(faopt1_2_cout));
  FAopt1 faopt1_3 (.B(B[5]), .Cin(faopt1_4_cout), .A(A[5]), .S(S[5]), .Cout(faopt1_3_cout));
  FAopt1 faopt1_4 (.B(B[4]), .Cin(faopt1_5_cout), .A(A[4]), .S(S[4]), .Cout(faopt1_4_cout));
  FAopt1 faopt1_5 (.B(B[3]), .Cin(faopt1_6_cout), .A(A[3]), .S(S[3]), .Cout(faopt1_5_cout));
  FAopt1 faopt1_6 (.B(B[2]), .Cin(faopt2_1_cout), .A(A[2]), .S(S[2]), .Cout(faopt1_6_cout));
  FAopt2 faopt2_1 (.B(B[1]), .Cin(fa0_1_c), .A(A[1]), .S(S[1]), .Cout(faopt2_1_cout));
  FA0 fa0_1 (.B(B[0]), .A(A[0]), .S(S[0]), .C(fa0_1_c));

  // Notes on the sheet:
  //   16
  //   14
  //   16.75
  //   16.75
  //   12
  //   14.75
  //   10
  //   12.75
  //   8
  //   10.75
  //   6
  //   8.75
  //   B6
  //   4
  //   6.75
  //   8.75
  //   8 Bit Ripple Adder
  //   Vishwa Kumaravel
  //   #248 Transistors
  //   5.5
  //   16.75
  //   16
  //   1.75
  //   2.75
endmodule

module two_to_one (
  input  in0,
  input  s,
  input  in1,
  output out_4
);

  wire nand_1_out, nand_2_out, not_1_out;

  not not_1 (not_1_out, s);
  nand nand_1 (nand_1_out, in0, not_1_out);
  nand nand_2 (nand_2_out, in1, s);
  nand nand_3 (out_4, nand_1_out, nand_2_out);

  // Notes on the sheet:
  //   z = max(s+2.75, in0+2, in1+2)
endmodule

module twotoonetransmission (
  input  in0,
  input  in1,
  input  s,
  output out_4
);

  wire not_1_out, transmission_1_p4;

  not not_1 (not_1_out, s);
  // Transmission_Gate transmission_1: pin names not known; wires that end beside it: in0, s, not_1_out, transmission_1_p4
  // Transmission_Gate transmission_2: pin names not known; wires that end beside it: in1, not_1_out, s, transmission_1_p4
  not not_2 (out_4, transmission_1_p4);

  // Notes on the sheet:
  //   z = max(s+1.75, in0+1, in1+1)
endmodule

module four_to_one (
  input  in0,
  input  in1,
  input  in2,
  input  in3,
  input  s0,
  input  s1,
  output out_7
);

  wire two_to_one_1_out_4, two_to_one_2_out_4;

  two_to_one two_to_one_1 (.in0(in0), .s(s0), .in1(in1), .out_4(two_to_one_1_out_4));
  two_to_one two_to_one_2 (.in0(in2), .s(s0), .in1(in3), .out_4(two_to_one_2_out_4));
  two_to_one two_to_one_3 (.in0(two_to_one_1_out_4), .s(s1), .in1(two_to_one_2_out_4), .out_4(out_7));

  // Notes on the sheet:
  //   z = max(s0+4.75, s1 + 2.75, in0+4, in1+4, in2 + 4, in3 + 4)
endmodule

module four_to_one_transmission (
  input  in0,
  input  in1,
  input  in2,
  input  in3,
  input  s0,
  input  s1,
  output out_7
);

  wire twotoonetransmission_1_out_4, twotoonetransmission_2_out_4;

  twotoonetransmission twotoonetransmission_1 (.in0(in0), .in1(in1), .s(s0), .out_4(twotoonetransmission_1_out_4));
  twotoonetransmission twotoonetransmission_2 (.in0(in2), .in1(in3), .s(s0), .out_4(twotoonetransmission_2_out_4));
  twotoonetransmission twotoonetransmission_3 (
    .in0(twotoonetransmission_1_out_4), .in1(twotoonetransmission_2_out_4), .s(s1), .out_4(out_7));

  // Notes on the sheet:
  //   z = max(s0+2.75, s1 + 1.75, in0+2, in1+2, in2 + 2, in3 + 2)
endmodule

module mx2i_4 (
  input  [3:0] in_1,
  input  [3:0] in_2,
  input  s,
  output [3:0] out_4
);

  twotoonetransmission twotoonetransmission_1 (.in0(in_1[0]), .in1(in_2[0]), .s(s), .out_4(out_4[0]));
  twotoonetransmission twotoonetransmission_2 (.in0(in_1[1]), .in1(in_2[1]), .s(s), .out_4(out_4[1]));
  twotoonetransmission twotoonetransmission_3 (.in0(in_1[2]), .in1(in_2[2]), .s(s), .out_4(out_4[2]));
  twotoonetransmission twotoonetransmission_4 (.in0(in_1[3]), .in1(in_2[3]), .s(s), .out_4(out_4[3]));
endmodule

module mx2i_8 (
  input  [7:0] A,
  input  [7:0] B,
  input  S,
  output [7:0] out_4
);

  mx2i_4 mx2i_4_1 (.s(S), .in_1(A[3:0]), .in_2(B[3:0]), .out_4(out_4[3:0]));
  mx2i_4 mx2i_4_2 (.s(S), .in_1(A[7:4]), .in_2(B[7:4]), .out_4(out_4[7:4]));
endmodule

module eight_bit_carry_0 (
  input  [7:0] in_1,
  input  [7:0] in_2,
  input  cin,
  output [7:0] S,
  output Cout
);

  wire fourbitadder0_1_cout, fourbitadder0_2_cout, fourbitadder1_1_cout, twotoonetransmission_1_out_4;
  wire [3:0] fourbitadder0_1_s, fourbitadder1_1_s, mx2i_4_1_out_4;

  twotoonetransmission twotoonetransmission_1 (
    .in0(fourbitadder0_1_cout), .in1(fourbitadder1_1_cout), .s(fourbitadder0_2_cout),
    .out_4(twotoonetransmission_1_out_4));
  FourBitAdder1 fourbitadder1_1 (.B(in_2[7:4]), .A(in_1[7:4]), .S(fourbitadder1_1_s), .cout(fourbitadder1_1_cout));
  mx2i_4 mx2i_4_1 (
    .s(fourbitadder0_2_cout), .in_1(fourbitadder0_1_s), .in_2(fourbitadder1_1_s), .out_4(mx2i_4_1_out_4));
  not not_1 (Cout, twotoonetransmission_1_out_4);
  FourBitAdder0 fourbitadder0_1 (
    .cin(1'b0), .B(in_2[7:4]), .A(in_1[7:4]), .S(fourbitadder0_1_s), .cout(fourbitadder0_1_cout));
  assign S[7:4] = ~mx2i_4_1_out_4;  // NOT_Gate not_2, 4 bits wide
  FourBitAdder0 fourbitadder0_2 (.cin(cin), .B(in_2[3:0]), .A(in_1[3:0]), .S(S[3:0]), .cout(fourbitadder0_2_cout));

  // Notes on the sheet:
  //   z=max(s+1.75, in0+1, in1+1)
  //   8
  //   9.75
  //   8.75
  //   8
  //   9.75
  //   8.75
  //   10.5
  //   8-Bit Carry Select Adder
  //   Vishwa Kumaravel
  //   8
  //   10.5
  //   8.75
  //   10.5
  //   10.5
endmodule

module eight_bit_carry_1 (
  input  [7:0] in_1,
  input  [7:0] in_2,
  output [7:0] S,
  output Cout
);

  wire fourbitadder0_1_cout, fourbitadder1_1_cout, fourbitadder1_2_cout, twotoonetransmission_1_out_4;
  wire [3:0] fourbitadder0_1_s, fourbitadder1_1_s, mx2i_4_1_out_4;

  twotoonetransmission twotoonetransmission_1 (
    .in0(fourbitadder0_1_cout), .in1(fourbitadder1_1_cout), .s(fourbitadder1_2_cout),
    .out_4(twotoonetransmission_1_out_4));
  FourBitAdder1 fourbitadder1_1 (.B(in_2[7:4]), .A(in_1[7:4]), .S(fourbitadder1_1_s), .cout(fourbitadder1_1_cout));
  mx2i_4 mx2i_4_1 (
    .s(fourbitadder1_2_cout), .in_1(fourbitadder0_1_s), .in_2(fourbitadder1_1_s), .out_4(mx2i_4_1_out_4));
  not not_1 (Cout, twotoonetransmission_1_out_4);
  FourBitAdder0 fourbitadder0_1 (
    .B(in_2[7:4]), .A(in_1[7:4]), .S(fourbitadder0_1_s), .cout(fourbitadder0_1_cout));  // open: cin
  assign S[7:4] = ~mx2i_4_1_out_4;  // NOT_Gate not_2, 4 bits wide
  FourBitAdder1 fourbitadder1_2 (.B(in_2[3:0]), .A(in_1[3:0]), .S(S[3:0]), .cout(fourbitadder1_2_cout));

  // Notes on the sheet:
  //   z=max(s+1.75, in0+1, in1+1)
  //   8
  //   9.75
  //   8.75
  //   8
  //   9.75
  //   10.5
  //   8.75
  //   8-Bit Carry Select Adder
  //   Vishwa Kumaravel
  //   8
  //   10.5
  //   8.75
  //   10.5
  //   10.5
endmodule

module sixteen_bit_carry (
  input  [15:0] inA,
  input  [15:0] inB,
  input  cin,
  output [15:0] S,
  output cout
);

  wire eight_bit_carry_0_1_cout, eight_bit_carry_0_2_cout, eight_bit_carry_1_1_cout,
       twotoonetransmission_1_out_4;
  wire [7:0] eight_bit_carry_0_1_s, eight_bit_carry_1_1_s, mx2i_8_1_out_4;

  twotoonetransmission twotoonetransmission_1 (
    .in0(eight_bit_carry_0_1_cout), .in1(eight_bit_carry_1_1_cout), .s(eight_bit_carry_0_2_cout),
    .out_4(twotoonetransmission_1_out_4));
  not not_1 (cout, twotoonetransmission_1_out_4);
  eight_bit_carry_1 eight_bit_carry_1_1 (
    .in_1(inA[15:8]), .in_2(inB[15:8]), .S(eight_bit_carry_1_1_s), .Cout(eight_bit_carry_1_1_cout));
  mx2i_8 mx2i_8_1 (
    .A(eight_bit_carry_0_1_s), .B(eight_bit_carry_1_1_s), .S(eight_bit_carry_0_2_cout), .out_4(mx2i_8_1_out_4));
  eight_bit_carry_0 eight_bit_carry_0_1 (
    .in_1(inA[15:8]), .in_2(inB[15:8]), .cin(1'b0), .S(eight_bit_carry_0_1_s), .Cout(eight_bit_carry_0_1_cout));
  assign S[15:8] = ~mx2i_8_1_out_4;  // NOT_Gate not_2, 8 bits wide
  eight_bit_carry_0 eight_bit_carry_0_2 (
    .in_1(inA[7:0]), .in_2(inB[7:0]), .cin(cin), .S(S[7:0]), .Cout(eight_bit_carry_0_2_cout));

  // Notes on the sheet:
  //   16 Bit Carry Select Adder
  //   Vishwa Kumaravel B6
  //   z=max(s+1.75, in0+1, in1+1)
  //   10.5
  //   12.25
  //   10.5
  //   13
  //   10.5
  //   10.5
  //   12.25
  //   10.5
  //   13
  //   10.5
  //   13
  //   13
endmodule

module adderSubtractor_70 (
  input  in_1,
  input  [15:0] in_2,
  input  [15:0] in_3,
  input  in_4,
  input  [15:0] in_5,
  input  [15:0] in_6,
  output [15:0] out_7,
  output [15:0] out_8
);

  wire sixteen_bit_carry_1_cout;
  wire [15:0] multiplexer_1_out, multiplexer_2_out, not_1_out, not_2_out;

  Multiplexer #(.width(16)) multiplexer_1 (.in0(in_3), .in1(not_1_out), .out(multiplexer_1_out), .sel(in_1));
  assign not_1_out = ~in_3;  // NOT_Gate not_1, 16 bits wide
  Multiplexer #(.width(16)) multiplexer_2 (.in0(in_6), .in1(not_2_out), .out(multiplexer_2_out), .sel(in_4));
  assign not_2_out = ~in_6;  // NOT_Gate not_2, 16 bits wide
  Adder #(.width(16)) adder_1 (.a(in_2), .b(multiplexer_1_out), .out(out_7), .cin(in_1));  // open: cout
  sixteen_bit_carry sixteen_bit_carry_1 (
    .inB(multiplexer_2_out), .inA(in_5), .cin(in_4), .S(out_8), .cout(sixteen_bit_carry_1_cout));
  // also tied to GND on the sheet: sixteen_bit_carry_1_cout
endmodule

module logismAdderSubtractor (
  input  op,
  input  [15:0] a,
  input  [15:0] b,
  output [15:0] s,
  output overflow
);

  wire nand_1_out, nand_2_out, not_2_out, not_3_out, not_4_out;
  wire [15:0] multiplexer_1_out, not_1_out;

  assign not_1_out = ~b;  // NOT_Gate not_1, 16 bits wide
  Multiplexer #(.width(16)) multiplexer_1 (.in0(b), .in1(not_1_out), .out(multiplexer_1_out), .sel(op));
  Adder #(.width(16)) adder_1 (.a(a), .b(multiplexer_1_out), .out(s), .cin(op));  // open: cout
  not not_2 (not_2_out, multiplexer_1_out[15]);
  not not_3 (not_3_out, a[15]);
  not not_4 (not_4_out, s[15]);
  nand nand_1 (nand_1_out, s[15], not_3_out, not_2_out);
  nand nand_2 (nand_2_out, a[15], not_4_out, multiplexer_1_out[15]);
  nand nand_3 (overflow, nand_1_out, nand_2_out);
endmodule

module CSA_Adder_Subtractor (
  input  op,
  input  [15:0] a,
  input  [15:0] b,
  output [15:0] s,
  output overflow
);

  wire nand_1_out, nand_2_out, not_2_out, not_3_out, not_4_out;
  wire [15:0] multiplexer_1_out, not_1_out;

  assign not_1_out = ~b;  // NOT_Gate not_1, 16 bits wide
  Multiplexer #(.width(16)) multiplexer_1 (.in0(b), .in1(not_1_out), .out(multiplexer_1_out), .sel(op));
  sixteen_bit_carry sixteen_bit_carry_1 (.inB(a), .inA(multiplexer_1_out), .cin(op), .S(s));  // open: cout
  not not_2 (not_2_out, multiplexer_1_out[15]);
  not not_3 (not_3_out, a[15]);
  not not_4 (not_4_out, s[15]);
  nand nand_1 (nand_1_out, s[15], not_3_out, not_2_out);
  nand nand_2 (nand_2_out, a[15], not_4_out, multiplexer_1_out[15]);
  nand nand_3 (overflow, nand_1_out, nand_2_out);
endmodule

module R0R1 (
  input  in_1,
  input  op,
  input  [15:0] in_3,
  output [15:0] out_4
);

  wire clk;
  wire [15:0] csa_adder_subtractor_1_s, R1_q;

  Clock clock_1 (.out(clk));
  Register #(.width(16)) R0 (.D(csa_adder_subtractor_1_s), .en(1'b1), .clk(clk), .Q(out_4), .clr(in_1));
  Register #(.width(16)) R1 (.D(in_3), .en(1'b1), .clk(clk), .Q(R1_q), .clr(in_1));
  Hex_Digit_Display hex_digit_display_1 (.value(out_4[15:12]));  // open: dp
  Hex_Digit_Display hex_digit_display_2 (.value(out_4[11:8]));  // open: dp
  Hex_Digit_Display hex_digit_display_3 (.value(out_4[7:4]));  // open: dp
  Hex_Digit_Display hex_digit_display_4 (.value(out_4[3:0]));  // open: dp
  CSA_Adder_Subtractor csa_adder_subtractor_1 (
    .a(out_4), .b(R1_q), .op(op), .s(csa_adder_subtractor_1_s));  // open: overflow

  // Other names for the same wires on the sheet: R0[15:0] = out_4; rst = in_1
endmodule

module regWe (
  input  [1:0] Rd,
  input  regWrite,
  output regWrite0,
  output regWrite1,
  output regWrite2,
  output regWrite3
);

  wire not_1_out, not_2_out;

  not not_1 (not_1_out, Rd[0]);
  not not_2 (not_2_out, Rd[1]);
  and and_1 (regWrite0, not_1_out, not_2_out, regWrite);
  and and_2 (regWrite1, Rd[0], not_2_out, regWrite);
  and and_3 (regWrite2, regWrite, Rd[1], not_1_out);
  and and_4 (regWrite3, Rd[0], Rd[1], regWrite);

  // Notes on the sheet:
  //   b
  //   a
endmodule

module srcSel (
  input  [15:0] reg0,
  input  [15:0] reg1,
  input  [15:0] reg2,
  input  [15:0] reg3,
  input  [1:0] sel,
  output [15:0] regOut
);

  Multiplexer #(.select(2), .width(16)) multiplexer_1 (
    .in0(reg0), .in1(reg1), .in2(reg2), .in3(reg3), .out(regOut), .sel(sel));
endmodule

module R2R3 (
  input  in_1,
  input  op,
  input  [1:0] in_3,
  input  [1:0] in_4,
  output [15:0] out_5,
  output [15:0] out_6,
  output [15:0] out_7,
  output [15:0] out_8
);

  wire clk, ovrfl, reg0WE, reg1WE, reg2WE, reg3WE, register_1_q;
  wire [15:0] csa_adder_subtractor_1_s, srcsel_1_regout, srcsel_2_regout;

  Clock clock_1 (.out(clk));
  Hex_Digit_Display hex_digit_display_1 (.value(out_5[15:12]));  // open: dp
  Hex_Digit_Display hex_digit_display_2 (.value(out_7[15:12]));  // open: dp
  Hex_Digit_Display hex_digit_display_3 (.value(out_5[11:8]));  // open: dp
  Hex_Digit_Display hex_digit_display_4 (.value(out_5[7:4]));  // open: dp
  Hex_Digit_Display hex_digit_display_5 (.value(out_7[11:8]));  // open: dp
  Hex_Digit_Display hex_digit_display_6 (.value(out_7[7:4]));  // open: dp
  Hex_Digit_Display hex_digit_display_7 (.value(out_5[3:0]));  // open: dp
  Hex_Digit_Display hex_digit_display_8 (.value(out_7[3:0]));  // open: dp
  srcSel srcsel_1 (.reg0(out_5), .reg1(out_6), .reg2(out_7), .reg3(out_8), .sel(in_4), .regOut(srcsel_1_regout));
  regWe regwe_1 (
    .Rd(in_3), .regWrite(1'b1), .regWrite0(reg0WE), .regWrite1(reg1WE), .regWrite2(reg2WE), .regWrite3(reg3WE));
  srcSel srcsel_2 (.reg0(out_5), .reg1(out_6), .reg2(out_7), .reg3(out_8), .sel(in_3), .regOut(srcsel_2_regout));
  Hex_Digit_Display hex_digit_display_9 (.value(out_6[15:12]));  // open: dp
  Hex_Digit_Display hex_digit_display_10 (.value(out_8[15:12]));  // open: dp
  Hex_Digit_Display hex_digit_display_11 (.value(out_6[11:8]));  // open: dp
  Hex_Digit_Display hex_digit_display_12 (.value(out_6[7:4]));  // open: dp
  Hex_Digit_Display hex_digit_display_13 (.value(out_8[11:8]));  // open: dp
  Hex_Digit_Display hex_digit_display_14 (.value(out_8[7:4]));  // open: dp
  Hex_Digit_Display hex_digit_display_15 (.value(out_6[3:0]));  // open: dp
  Hex_Digit_Display hex_digit_display_16 (.value(out_8[3:0]));  // open: dp
  CSA_Adder_Subtractor csa_adder_subtractor_1 (
    .a(srcsel_2_regout), .b(srcsel_1_regout), .op(op), .s(csa_adder_subtractor_1_s), .overflow(ovrfl));
  Register #(.width(1)) register_1 (.D(1'b1), .en(ovrfl), .clk(clk), .Q(register_1_q), .clr(in_1));
  LED led_1 (.in(register_1_q));
  Register #(.width(16)) R0 (.D(csa_adder_subtractor_1_s), .en(reg0WE), .clk(clk), .Q(out_5), .clr(in_1));
  Register #(.width(16)) R1 (.D(csa_adder_subtractor_1_s), .en(reg1WE), .clk(clk), .Q(out_6), .clr(in_1));
  Register #(.width(16)) R2 (.D(csa_adder_subtractor_1_s), .en(reg2WE), .clk(clk), .Q(out_7), .clr(in_1));
  Register #(.width(16)) R3 (.D(csa_adder_subtractor_1_s), .en(reg3WE), .clk(clk), .Q(out_8), .clr(in_1));

  // Other names for the same wires on the sheet: R0[15:0] = out_5; R1[15:0] = out_6; R2[15:0] = out_7;
  //   R3[15:0] = out_8; Rd[1:0] = in_3; Rs[1:0] = in_4; rst = in_1

  // Notes on the sheet:
  //   LA: 4c41
  //   SA: 5341
  //   C : 7b43
  //   S: 537D
endmodule

module programCounter (
  input  in_1,
  input  in_2,
  output [5:0] out_3
);

  wire [5:0] adder_1_out;

  Register #(.width(6)) register_1 (.D(adder_1_out), .clk(in_1), .Q(out_3), .clr(in_2));  // open: en
  Adder #(.width(6)) adder_1 (.a(6'b000001), .b(out_3), .out(adder_1_out));  // open: cin, cout
endmodule

module program_memory (
  input  in_1,
  output [15:0] out_2,
  output [15:0] out_3,
  output [15:0] out_4,
  output [15:0] out_5
);

  wire clk, op, ovrfl, reg0WE, reg1WE, reg2WE, reg3WE, register_1_q;
  wire [1:0] Rd, Rs;
  wire [3:0] ram_1_dout;
  wire [5:0] programcounter_1_out_3;
  wire [15:0] csa_adder_subtractor_1_s, srcsel_1_regout, srcsel_2_regout;

  Clock clock_1 (.out(clk));
  Hex_Digit_Display hex_digit_display_1 (.value(out_2[15:12]));  // open: dp
  Hex_Digit_Display hex_digit_display_2 (.value(out_4[15:12]));  // open: dp
  Hex_Digit_Display hex_digit_display_3 (.value(out_2[11:8]));  // open: dp
  Hex_Digit_Display hex_digit_display_4 (.value(out_2[7:4]));  // open: dp
  Hex_Digit_Display hex_digit_display_5 (.value(out_4[11:8]));  // open: dp
  Hex_Digit_Display hex_digit_display_6 (.value(out_4[7:4]));  // open: dp
  Hex_Digit_Display hex_digit_display_7 (.value(out_2[3:0]));  // open: dp
  Hex_Digit_Display hex_digit_display_8 (.value(out_4[3:0]));  // open: dp
  srcSel srcsel_1 (.reg0(out_2), .reg1(out_3), .reg2(out_4), .reg3(out_5), .sel(Rs), .regOut(srcsel_1_regout));
  regWe regwe_1 (
    .Rd(Rd), .regWrite(1'b1), .regWrite0(reg0WE), .regWrite1(reg1WE), .regWrite2(reg2WE), .regWrite3(reg3WE));
  srcSel srcsel_2 (.reg0(out_2), .reg1(out_3), .reg2(out_4), .reg3(out_5), .sel(Rd), .regOut(srcsel_2_regout));
  Hex_Digit_Display hex_digit_display_9 (.value(out_3[15:12]));  // open: dp
  Hex_Digit_Display hex_digit_display_10 (.value(out_5[15:12]));  // open: dp
  Register #(.width(1)) register_1 (.D(1'b1), .en(ovrfl), .clk(clk), .Q(register_1_q), .clr(in_1));
  Hex_Digit_Display hex_digit_display_11 (.value(out_3[11:8]));  // open: dp
  Hex_Digit_Display hex_digit_display_12 (.value(out_3[7:4]));  // open: dp
  Hex_Digit_Display hex_digit_display_13 (.value(out_5[11:8]));  // open: dp
  Hex_Digit_Display hex_digit_display_14 (.value(out_5[7:4]));  // open: dp
  Hex_Digit_Display hex_digit_display_15 (.value(out_3[3:0]));  // open: dp
  Hex_Digit_Display hex_digit_display_16 (.value(out_5[3:0]));  // open: dp
  LED led_1 (.in(register_1_q));
  CSA_Adder_Subtractor csa_adder_subtractor_1 (
    .a(srcsel_2_regout), .b(srcsel_1_regout), .op(op), .s(csa_adder_subtractor_1_s), .overflow(ovrfl));
  Register #(.width(16)) R0 (.D(csa_adder_subtractor_1_s), .en(reg0WE), .clk(clk), .Q(out_2), .clr(in_1));
  Register #(.width(16)) R1 (.D(csa_adder_subtractor_1_s), .en(reg1WE), .clk(clk), .Q(out_3), .clr(in_1));
  Register #(.width(16)) R2 (.D(csa_adder_subtractor_1_s), .en(reg2WE), .clk(clk), .Q(out_4), .clr(in_1));
  Register #(.width(16)) R3 (.D(csa_adder_subtractor_1_s), .en(reg3WE), .clk(clk), .Q(out_5), .clr(in_1));
  programCounter programcounter_1 (.in_1(clk), .in_2(in_1), .out_3(programcounter_1_out_3));
  RAM #(.addrWidth(6), .asyncread("true"), .trigger("falling")) ram_1 (
    .addr(programcounter_1_out_3), .we(1'b0), .oe(1'b1), .clk(clk), .dout({Rd, Rs, ram_1_dout}));  // open: din
  and and_1 (op, ram_1_dout[0], ram_1_dout[1]);

  // Other names for the same wires on the sheet: R0[15:0] = out_2; R1[15:0] = out_3; R2[15:0] = out_4;
  //   R3[15:0] = out_5; rst = in_1

  // Notes on the sheet:
  //   LA: 4c41
  //   SA: 5341
  //   C : 7b43
  //   S: 537D
  //   B3, 43, E2, 32, 82
endmodule

module IRDecoder (
  input  [7:0] IR,
  input  clk,
  input  rst,
  output sub,
  output [1:0] Rs,
  output [1:0] Rd
);

  wire and_1_out;

  Register #(.width(2)) register_1 (.D(IR[5:4]), .clk(clk), .Q(Rs), .clr(rst));  // open: en
  Register #(.width(2)) register_2 (.D(IR[7:6]), .clk(clk), .Q(Rd), .clr(rst));  // open: en
  and and_1 (and_1_out, IR[0], IR[1]);
  Register #(.width(1)) register_3 (.D(and_1_out), .clk(clk), .Q(sub), .clr(rst));  // open: en
endmodule

module IR (
  input  in_1,
  output [15:0] out_2,
  output [15:0] out_3,
  output [15:0] out_4,
  output [15:0] out_5
);

  wire clk, op, ovrfl, reg0WE, reg1WE, reg2WE, reg3WE, register_1_q, register_3_q, regWrite;
  wire [1:0] Rd, Rs;
  wire [3:0] register_4_q, register_4_q_2, register_5_q, register_5_q_2, register_6_q, register_6_q_2;
  wire [5:0] programcounter_1_out_3;
  wire [7:0] ram_1_dout;
  wire [15:0] csa_adder_subtractor_1_s, srcsel_1_regout, srcsel_2_regout;

  Clock clock_1 (.out(clk));
  Register #(.width(1)) register_1 (.D(1'b1), .en(1'b1), .clk(clk), .Q(register_1_q), .clr(in_1));
  Hex_Digit_Display hex_digit_display_1 (.value(out_2[15:12]));  // open: dp
  Hex_Digit_Display hex_digit_display_2 (.value(out_4[15:12]));  // open: dp
  Register #(.width(1)) register_2 (.D(register_1_q), .en(1'b1), .clk(clk), .Q(regWrite), .clr(in_1));
  Hex_Digit_Display hex_digit_display_3 (.value(out_2[11:8]));  // open: dp
  Hex_Digit_Display hex_digit_display_4 (.value(out_2[7:4]));  // open: dp
  Hex_Digit_Display hex_digit_display_5 (.value(out_4[11:8]));  // open: dp
  Hex_Digit_Display hex_digit_display_6 (.value(out_4[7:4]));  // open: dp
  Hex_Digit_Display hex_digit_display_7 (.value(out_2[3:0]));  // open: dp
  Hex_Digit_Display hex_digit_display_8 (.value(out_4[3:0]));  // open: dp
  srcSel srcsel_1 (.reg0(out_2), .reg1(out_3), .reg2(out_4), .reg3(out_5), .sel(Rs), .regOut(srcsel_1_regout));
  regWe regwe_1 (
    .Rd(Rd), .regWrite(regWrite), .regWrite0(reg0WE), .regWrite1(reg1WE), .regWrite2(reg2WE),
    .regWrite3(reg3WE));
  srcSel srcsel_2 (.reg0(out_2), .reg1(out_3), .reg2(out_4), .reg3(out_5), .sel(Rd), .regOut(srcsel_2_regout));
  Hex_Digit_Display hex_digit_display_9 (.value(out_3[15:12]));  // open: dp
  Hex_Digit_Display hex_digit_display_10 (.value(out_5[15:12]));  // open: dp
  Register #(.width(1)) register_3 (.D(regWrite), .en(ovrfl), .clk(clk), .Q(register_3_q), .clr(in_1));
  Hex_Digit_Display hex_digit_display_11 (.value(out_3[11:8]));  // open: dp
  Hex_Digit_Display hex_digit_display_12 (.value(out_3[7:4]));  // open: dp
  Hex_Digit_Display hex_digit_display_13 (.value(out_5[11:8]));  // open: dp
  Hex_Digit_Display hex_digit_display_14 (.value(out_5[7:4]));  // open: dp
  Hex_Digit_Display hex_digit_display_15 (.value(out_3[3:0]));  // open: dp
  Hex_Digit_Display hex_digit_display_16 (.value(out_5[3:0]));  // open: dp
  LED led_1 (.in(register_3_q));
  CSA_Adder_Subtractor csa_adder_subtractor_1 (
    .a(srcsel_2_regout), .b(srcsel_1_regout), .op(op), .s(csa_adder_subtractor_1_s), .overflow(ovrfl));
  Register #(.width(16)) R0 (.D(csa_adder_subtractor_1_s), .en(reg0WE), .clk(clk), .Q(out_2), .clr(in_1));
  Register #(.width(16)) R1 (.D(csa_adder_subtractor_1_s), .en(reg1WE), .clk(clk), .Q(out_3), .clr(in_1));
  Register #(.width(16)) R2 (.D(csa_adder_subtractor_1_s), .en(reg2WE), .clk(clk), .Q(out_4), .clr(in_1));
  Register #(.width(16)) R3 (.D(csa_adder_subtractor_1_s), .en(reg3WE), .clk(clk), .Q(out_5), .clr(in_1));
  programCounter programcounter_1 (.in_1(clk), .in_2(in_1), .out_3(programcounter_1_out_3));
  RAM #(.addrWidth(6), .asyncread("true"), .trigger("falling")) ram_1 (
    .addr(programcounter_1_out_3), .we(1'b0), .oe(1'b1), .clk(clk), .dout(ram_1_dout));  // open: din
  Register register_4 (.D(ram_1_dout), .en(1'b1), .clk(clk), .Q({register_4_q_2, register_4_q}), .clr(in_1));
  Hex_Digit_Display hex_digit_display_17 (.value(register_4_q_2));  // open: dp
  Hex_Digit_Display hex_digit_display_18 (.value(register_4_q));  // open: dp
  Register register_5 (
    .D({register_4_q_2, register_4_q}), .en(1'b1), .clk(clk), .Q({register_5_q_2, register_5_q}), .clr(in_1));
  Hex_Digit_Display hex_digit_display_19 (.value(register_5_q_2));  // open: dp
  Hex_Digit_Display hex_digit_display_20 (.value(register_5_q));  // open: dp
  Register register_6 (
    .D({register_5_q_2, register_5_q}), .en(1'b1), .clk(clk), .Q({register_6_q_2, register_6_q}), .clr(in_1));
  IRDecoder irdecoder_1 (.IR({register_4_q_2, register_4_q}), .clk(clk), .rst(in_1), .sub(op), .Rs(Rs), .Rd(Rd));
  Hex_Digit_Display hex_digit_display_21 (.value(register_6_q_2));  // open: dp
  Hex_Digit_Display hex_digit_display_22 (.value(register_6_q));  // open: dp

  // Other names for the same wires on the sheet: R0[15:0] = out_2; R1[15:0] = out_3; R2[15:0] = out_4;
  //   R3[15:0] = out_5; rst = in_1

  // Notes on the sheet:
  //   LA: 4c41
  //   SA: 5341
  //   C : 7b43
  //   S: 537D
  //   B3, 43, E2, 32, 82
  //   Instruction Register
endmodule

module IRDecoderAgain (
  input  [7:0] in_1,
  input  clk,
  input  rst,
  output op,
  output [1:0] Rs,
  output [1:0] Rd,
  output loadimmediate,
  output load
);

  wire and_1_out, and_2_out, and_3_out, not_1_out, not_2_out, not_3_out;

  Register #(.width(2)) register_1 (.D(in_1[5:4]), .clk(clk), .Q(Rs), .clr(rst));  // open: en
  Register #(.width(2)) register_2 (.D(in_1[7:6]), .clk(clk), .Q(Rd), .clr(rst));  // open: en
  not not_1 (not_1_out, in_1[0]);
  and and_1 (and_1_out, in_1[0], in_1[1], in_1[2], in_1[3]);
  and and_2 (and_2_out, in_1[3], in_1[2], in_1[1], not_1_out);
  and and_3 (and_3_out, in_1[0], in_1[1], not_2_out, not_3_out);
  not not_2 (not_2_out, in_1[2]);
  not not_3 (not_3_out, in_1[3]);
  D_Flip_Flop d_ff_1 (.D(and_2_out), .clk(clk), .Q(loadimmediate), .reset(rst));  // open: Qn, preset
  D_Flip_Flop d_ff_2 (.D(and_1_out), .clk(clk), .Q(load), .reset(rst));  // open: Qn, preset
  D_Flip_Flop d_ff_3 (.D(and_3_out), .clk(clk), .Q(op), .reset(rst));  // open: Qn, preset
endmodule

module loadData (
  input  in_1,
  output [15:0] out_2,
  output [15:0] out_3,
  output [15:0] out_4,
  output [15:0] out_5
);

  wire clk, ld, ldi, op, ovrfl, reg0WE, reg1WE, reg2WE, reg3WE, register_1_q, register_3_q, regWrite;
  wire [1:0] Rd, Rs;
  wire [3:0] register_4_q, register_4_q_2, register_5_q, register_5_q_2, register_6_q, register_6_q_2;
  wire [5:0] programcounter_1_out_3;
  wire [7:0] ram_1_dout;
  wire [15:0] InB, multiplexer_1_out, outpt, ram_2_dout, srcsel_2_regout, sum;

  Clock clock_1 (.out(clk));
  Register #(.width(1)) register_1 (.D(1'b1), .en(1'b1), .clk(clk), .Q(register_1_q), .clr(in_1));
  Hex_Digit_Display hex_digit_display_1 (.value(out_2[15:12]));  // open: dp
  Hex_Digit_Display hex_digit_display_2 (.value(out_4[15:12]));  // open: dp
  Register #(.width(1)) register_2 (.D(register_1_q), .en(1'b1), .clk(clk), .Q(regWrite), .clr(in_1));
  Hex_Digit_Display hex_digit_display_3 (.value(out_2[11:8]));  // open: dp
  Hex_Digit_Display hex_digit_display_4 (.value(out_2[7:4]));  // open: dp
  Hex_Digit_Display hex_digit_display_5 (.value(out_4[11:8]));  // open: dp
  Hex_Digit_Display hex_digit_display_6 (.value(out_4[7:4]));  // open: dp
  Hex_Digit_Display hex_digit_display_7 (.value(out_2[3:0]));  // open: dp
  Hex_Digit_Display hex_digit_display_8 (.value(out_4[3:0]));  // open: dp
  srcSel srcsel_1 (.reg0(out_2), .reg1(out_3), .reg2(out_4), .reg3(out_5), .sel(Rs), .regOut(InB));
  regWe regwe_1 (
    .Rd(Rd), .regWrite(regWrite), .regWrite0(reg0WE), .regWrite1(reg1WE), .regWrite2(reg2WE),
    .regWrite3(reg3WE));
  srcSel srcsel_2 (.reg0(out_2), .reg1(out_3), .reg2(out_4), .reg3(out_5), .sel(Rd), .regOut(srcsel_2_regout));
  Hex_Digit_Display hex_digit_display_9 (.value(out_3[15:12]));  // open: dp
  Hex_Digit_Display hex_digit_display_10 (.value(out_5[15:12]));  // open: dp
  Register #(.width(1)) register_3 (.D(regWrite), .en(ovrfl), .clk(clk), .Q(register_3_q), .clr(in_1));
  Hex_Digit_Display hex_digit_display_11 (.value(out_3[11:8]));  // open: dp
  Hex_Digit_Display hex_digit_display_12 (.value(out_3[7:4]));  // open: dp
  Hex_Digit_Display hex_digit_display_13 (.value(out_5[11:8]));  // open: dp
  Hex_Digit_Display hex_digit_display_14 (.value(out_5[7:4]));  // open: dp
  Hex_Digit_Display hex_digit_display_15 (.value(out_3[3:0]));  // open: dp
  Hex_Digit_Display hex_digit_display_16 (.value(out_5[3:0]));  // open: dp
  LED led_1 (.in(register_3_q));
  CSA_Adder_Subtractor csa_adder_subtractor_1 (.a(srcsel_2_regout), .b(InB), .op(op), .s(sum), .overflow(ovrfl));
  Register #(.width(16)) R0 (.D(outpt), .en(reg0WE), .clk(clk), .Q(out_2), .clr(in_1));
  Register #(.width(16)) R1 (.D(outpt), .en(reg1WE), .clk(clk), .Q(out_3), .clr(in_1));
  Register #(.width(16)) R2 (.D(outpt), .en(reg2WE), .clk(clk), .Q(out_4), .clr(in_1));
  Register #(.width(16)) R3 (.D(outpt), .en(reg3WE), .clk(clk), .Q(out_5), .clr(in_1));
  programCounter programcounter_1 (.in_1(clk), .in_2(in_1), .out_3(programcounter_1_out_3));
  RAM #(.addrWidth(6), .asyncread("true"), .trigger("falling")) ram_1 (
    .addr(programcounter_1_out_3), .we(1'b0), .oe(1'b1), .clk(clk), .dout(ram_1_dout));  // open: din
  RAM #(.addrWidth(4), .asyncread("true"), .dataWidth(16), .trigger("falling")) ram_2 (
    .addr(InB[3:0]), .we(1'b0), .oe(1'b1), .clk(clk), .dout(ram_2_dout));  // open: din
  Multiplexer #(.width(16)) multiplexer_1 (.in0(sum), .in1(ram_2_dout), .out(multiplexer_1_out), .sel(ld));
  Register register_4 (.D(ram_1_dout), .en(1'b1), .clk(clk), .Q({register_4_q_2, register_4_q}), .clr(in_1));
  Multiplexer #(.width(16)) multiplexer_2 (.in0(multiplexer_1_out), .in1({{14{1'b0}}, Rs}), .out(outpt), .sel(ldi));
  Hex_Digit_Display hex_digit_display_17 (.value(register_4_q_2));  // open: dp
  Hex_Digit_Display hex_digit_display_18 (.value(register_4_q));  // open: dp
  Register register_5 (
    .D({register_4_q_2, register_4_q}), .en(1'b1), .clk(clk), .Q({register_5_q_2, register_5_q}), .clr(in_1));
  Hex_Digit_Display hex_digit_display_19 (.value(register_5_q_2));  // open: dp
  Hex_Digit_Display hex_digit_display_20 (.value(register_5_q));  // open: dp
  Register register_6 (
    .D({register_5_q_2, register_5_q}), .en(1'b1), .clk(clk), .Q({register_6_q_2, register_6_q}), .clr(in_1));
  Hex_Digit_Display hex_digit_display_21 (.value(register_6_q_2));  // open: dp
  IRDecoderAgain irdecoderagain_1 (
    .in_1({register_4_q_2, register_4_q}), .clk(clk), .rst(in_1), .op(op), .Rs(Rs), .Rd(Rd),
    .loadimmediate(ldi), .load(ld));
  Hex_Digit_Display hex_digit_display_22 (.value(register_6_q));  // open: dp

  // Other names for the same wires on the sheet: R0[15:0] = out_2; R1[15:0] = out_3; R2[15:0] = out_4;
  //   R3[15:0] = out_5; rst = in_1

  // Notes on the sheet:
  //   LA: 4c41
  //   SA: 5341
  //   C : 7b43
  //   S: 537D
  //   B3, 43, E2, 32, 82
  //   Instruction Register
endmodule

module IRFibbo (
  input  [7:0] IR,
  input  clk,
  input  rst,
  output op,
  output move,
  output [1:0] Rs,
  output store,
  output [1:0] Rd,
  output loadimmediate,
  output load
);

  wire and_1_out, and_2_out, and_3_out, and_4_out, and_5_out, not_1_out, not_2_out, not_3_out, not_4_out,
       not_5_out, not_6_out;

  Register #(.width(2)) register_1 (.D(IR[5:4]), .clk(clk), .Q(Rs), .clr(rst));  // open: en
  Register #(.width(2)) register_2 (.D(IR[7:6]), .clk(clk), .Q(Rd), .clr(rst));  // open: en
  not not_1 (not_1_out, IR[0]);
  and and_1 (and_1_out, IR[0], IR[1], IR[2], IR[3]);
  not not_2 (not_2_out, IR[2]);
  and and_2 (and_2_out, IR[3], IR[2], IR[1], not_1_out);
  and and_3 (and_3_out, IR[0], IR[1], not_3_out, not_4_out);
  not not_3 (not_3_out, IR[2]);
  not not_4 (not_4_out, IR[3]);
  not not_5 (not_5_out, IR[1]);
  and and_4 (and_4_out, IR[0], not_5_out, IR[2], not_6_out);
  not not_6 (not_6_out, IR[3]);
  and and_5 (and_5_out, IR[3], not_2_out, IR[1], IR[0]);
  D_Flip_Flop d_ff_1 (.D(and_2_out), .clk(clk), .Q(loadimmediate), .reset(rst));  // open: Qn, preset
  D_Flip_Flop d_ff_2 (.D(and_1_out), .clk(clk), .Q(load), .reset(rst));  // open: Qn, preset
  D_Flip_Flop d_ff_3 (.D(and_3_out), .clk(clk), .Q(op), .reset(rst));  // open: Qn, preset
  D_Flip_Flop d_ff_4 (.D(and_4_out), .clk(clk), .Q(move), .reset(rst));  // open: Qn, preset
  D_Flip_Flop d_ff_5 (.D(and_5_out), .clk(clk), .Q(store), .reset(rst));  // open: Qn, preset
endmodule

module fibbonacci (
  input  in_1,
  input  in_2,
  output [15:0] out_3,
  output [15:0] out_4,
  output [15:0] out_5,
  output [15:0] out_6
);

  wire clk, ld, ldi, not_1_out, op, ovrfl, reg0WE, reg1WE, reg2WE, reg3WE, register_1_q, register_2_q,
       register_3_q, regWrite, store;
  wire [1:0] Rd, Rs;
  wire [3:0] register_4_q, register_4_q_2, register_5_q, register_5_q_2, register_6_q, register_6_q_2;
  wire [5:0] programcounter_1_out_3;
  wire [7:0] ram_1_dout;
  wire [15:0] InB, multiplexer_2_out, outpt, ram_2_dout, srcsel_2_regout, srcsel_3_regout, sum;

  Clock clock_1 (.out(clk));
  Register #(.width(1)) register_1 (.D(1'b1), .en(1'b1), .clk(clk), .Q(register_1_q), .clr(in_1));
  Hex_Digit_Display hex_digit_display_1 (.value(out_3[15:12]));  // open: dp
  Hex_Digit_Display hex_digit_display_2 (.value(out_5[15:12]));  // open: dp
  Register #(.width(1)) register_2 (.D(register_1_q), .en(1'b1), .clk(clk), .Q(register_2_q), .clr(in_1));
  Hex_Digit_Display hex_digit_display_3 (.value(out_3[11:8]));  // open: dp
  Hex_Digit_Display hex_digit_display_4 (.value(out_3[7:4]));  // open: dp
  Hex_Digit_Display hex_digit_display_5 (.value(out_5[11:8]));  // open: dp
  Hex_Digit_Display hex_digit_display_6 (.value(out_5[7:4]));  // open: dp
  Multiplexer multiplexer_1 (.in0(register_2_q), .in1(in_2), .out(regWrite), .sel(store));
  Hex_Digit_Display hex_digit_display_7 (.value(out_3[3:0]));  // open: dp
  Hex_Digit_Display hex_digit_display_8 (.value(out_5[3:0]));  // open: dp
  srcSel srcsel_1 (.reg0(out_3), .reg1(out_4), .reg2(out_5), .reg3(out_6), .sel(Rs), .regOut(InB));
  regWe regwe_1 (
    .Rd(Rd), .regWrite(regWrite), .regWrite0(reg0WE), .regWrite1(reg1WE), .regWrite2(reg2WE),
    .regWrite3(reg3WE));
  srcSel srcsel_2 (.reg0(out_3), .reg1(out_4), .reg2(out_5), .reg3(out_6), .sel(Rd), .regOut(srcsel_2_regout));
  Hex_Digit_Display hex_digit_display_9 (.value(out_4[15:12]));  // open: dp
  Hex_Digit_Display hex_digit_display_10 (.value(out_6[15:12]));  // open: dp
  Register #(.width(1)) register_3 (.D(regWrite), .en(ovrfl), .clk(clk), .Q(register_3_q), .clr(in_1));
  Hex_Digit_Display hex_digit_display_11 (.value(out_4[11:8]));  // open: dp
  Hex_Digit_Display hex_digit_display_12 (.value(out_4[7:4]));  // open: dp
  Hex_Digit_Display hex_digit_display_13 (.value(out_6[11:8]));  // open: dp
  Hex_Digit_Display hex_digit_display_14 (.value(out_6[7:4]));  // open: dp
  Hex_Digit_Display hex_digit_display_15 (.value(out_4[3:0]));  // open: dp
  Hex_Digit_Display hex_digit_display_16 (.value(out_6[3:0]));  // open: dp
  LED led_1 (.in(register_3_q));
  CSA_Adder_Subtractor csa_adder_subtractor_1 (.a(srcsel_2_regout), .b(InB), .op(op), .s(sum), .overflow(ovrfl));
  not not_1 (not_1_out, store);
  srcSel srcsel_3 (.reg0(out_3), .reg1(out_4), .reg2(out_5), .reg3(out_6), .sel(Rd), .regOut(srcsel_3_regout));
  Register #(.width(16)) R0 (.D(outpt), .en(reg0WE), .clk(clk), .Q(out_3), .clr(in_1));
  Register #(.width(16)) R1 (.D(outpt), .en(reg1WE), .clk(clk), .Q(out_4), .clr(in_1));
  Register #(.width(16)) R2 (.D(outpt), .en(reg2WE), .clk(clk), .Q(out_5), .clr(in_1));
  Register #(.width(16)) R3 (.D(outpt), .en(reg3WE), .clk(clk), .Q(out_6), .clr(in_1));
  programCounter programcounter_1 (.in_1(clk), .in_2(in_1), .out_3(programcounter_1_out_3));
  RAM #(.addrWidth(6), .asyncread("true"), .trigger("falling")) ram_1 (
    .addr(programcounter_1_out_3), .we(1'b0), .oe(1'b1), .clk(clk), .dout(ram_1_dout));  // open: din
  RAM #(.addrWidth(4), .asyncread("true"), .dataWidth(16), .trigger("falling")) ram_2 (
    .addr(InB[3:0]), .we(store), .oe(not_1_out), .clk(clk), .din(srcsel_3_regout), .dout(ram_2_dout));
  Multiplexer #(.width(16)) multiplexer_2 (.in0(sum), .in1(ram_2_dout), .out(multiplexer_2_out), .sel(ld));
  Register register_4 (.D(ram_1_dout), .en(1'b1), .clk(clk), .Q({register_4_q_2, register_4_q}), .clr(in_1));
  Multiplexer #(.width(16)) multiplexer_3 (.in0(multiplexer_2_out), .in1({{14{1'b0}}, Rs}), .out(outpt), .sel(ldi));
  Hex_Digit_Display hex_digit_display_17 (.value(register_4_q_2));  // open: dp
  Hex_Digit_Display hex_digit_display_18 (.value(register_4_q));  // open: dp
  Register register_5 (
    .D({register_4_q_2, register_4_q}), .en(1'b1), .clk(clk), .Q({register_5_q_2, register_5_q}), .clr(in_1));
  Hex_Digit_Display hex_digit_display_19 (.value(register_5_q_2));  // open: dp
  Hex_Digit_Display hex_digit_display_20 (.value(register_5_q));  // open: dp
  Register register_6 (
    .D({register_5_q_2, register_5_q}), .en(1'b1), .clk(clk), .Q({register_6_q_2, register_6_q}), .clr(in_1));
  Hex_Digit_Display hex_digit_display_21 (.value(register_6_q_2));  // open: dp
  IRFibbo irfibbo_1 (
    .IR({register_4_q_2, register_4_q}), .clk(clk), .rst(in_1), .op(op), .Rs(Rs), .store(store), .Rd(Rd),
    .loadimmediate(ldi), .load(ld));  // open: move
  Hex_Digit_Display hex_digit_display_22 (.value(register_6_q));  // open: dp

  // Other names for the same wires on the sheet: R0[15:0] = out_3; R1[15:0] = out_4; R2[15:0] = out_5;
  //   R3[15:0] = out_6; rst = in_1

  // Notes on the sheet:
  //   LA: 4c41
  //   SA: 5341
  //   C : 7b43
  //   S: 537D
  //   B3, 43, E2, 32, 82
  //   Instruction Register
endmodule

module IRPipeline (
  input  [7:0] IR,
  input  clk,
  input  rst,
  output [7:0] instruction,
  output op,
  output move,
  output [1:0] Rs,
  output store,
  output [1:0] Rd,
  output loadimmediate,
  output load,
  output halt,
  output jump,
  output [5:0] target
);

  wire and_1_out, and_2_out, and_3_out, and_4_out, and_5_out, and_6_out, and_7_out, nor_1_out, not_1_out,
       not_2_out, not_3_out, not_4_out, not_5_out, not_6_out, not_7_out, not_8_out;

  Register #(.width(2)) register_1 (.D(IR[5:4]), .clk(clk), .Q(Rs), .clr(rst));  // open: en
  Register #(.width(2)) register_2 (.D(IR[7:6]), .clk(clk), .Q(Rd), .clr(rst));  // open: en
  Register #(.width(6)) register_3 (.D(IR[7:2]), .clk(clk), .Q(target), .clr(rst));  // open: en
  Register register_4 (.D(IR), .en(clk), .clk(1'b1), .Q(instruction), .clr(rst));
  not not_1 (not_1_out, IR[0]);
  and and_1 (and_1_out, IR[0], IR[1], IR[2], IR[3]);
  nor nor_1 (nor_1_out, IR[0], IR[1]);
  not not_2 (not_2_out, IR[2]);
  and and_2 (and_2_out, IR[3], IR[2], IR[1], not_1_out);
  and and_3 (and_3_out, IR[0], IR[1], not_3_out, not_4_out);
  not not_3 (not_3_out, IR[2]);
  not not_4 (not_4_out, IR[3]);
  not not_5 (not_5_out, IR[0]);
  and and_4 (and_4_out, not_5_out, IR[1], IR[2], not_6_out);
  not not_6 (not_6_out, IR[3]);
  and and_5 (and_5_out, IR[3], not_2_out, IR[1], IR[0]);
  D_Flip_Flop d_ff_1 (.D(and_2_out), .clk(clk), .Q(loadimmediate), .reset(rst));  // open: Qn, preset
  D_Flip_Flop d_ff_2 (.D(and_1_out), .clk(clk), .Q(load), .reset(rst));  // open: Qn, preset
  D_Flip_Flop d_ff_3 (.D(and_3_out), .clk(clk), .Q(op), .reset(rst));  // open: Qn, preset
  D_Flip_Flop d_ff_4 (.D(and_4_out), .clk(clk), .Q(move), .reset(rst));  // open: Qn, preset
  D_Flip_Flop d_ff_5 (.D(and_5_out), .clk(clk), .Q(store), .reset(rst));  // open: Qn, preset
  Register #(.width(1)) register_5 (.D(nor_1_out), .clk(clk), .Q(jump), .clr(rst));  // open: en
  not not_7 (not_7_out, IR[0]);
  and and_6 (and_6_out, not_7_out, IR[1], IR[2], not_8_out);
  not not_8 (not_8_out, IR[3]);
  and and_7 (and_7_out, and_6_out, IR[4], IR[5], IR[6], IR[7]);
  D_Flip_Flop d_ff_6 (.D(and_7_out), .clk(clk), .Q(halt), .reset(rst));  // open: Qn, preset

  // Other names for the same wires on the sheet: bit0 = IR[4]; bit1 = IR[5]; bit2 = IR[6]; bit3 = IR[7]
endmodule

module programCounter2 (
  input  [5:0] target,
  input  jump,
  input  clk,
  input  rst,
  output [5:0] loc
);

  wire [5:0] adder_1_out, multiplexer_1_out;

  Register #(.width(6)) register_1 (.D(multiplexer_1_out), .clk(clk), .Q(loc), .clr(rst));  // open: en
  Multiplexer #(.width(6)) multiplexer_1 (.in0(adder_1_out), .in1(target), .out(multiplexer_1_out), .sel(jump));
  Adder #(.width(6)) adder_1 (.a(6'b000001), .b(loc), .out(adder_1_out));  // open: cin, cout
endmodule

module pipeline (
  input  in_1,
  output [15:0] out_2,
  output [15:0] out_3,
  output [5:0] out_4,
  output [15:0] out_5,
  output [15:0] out_6
);

  wire clk, halt, jmp, ld, ldi, move, not_1_out, not_2_out, not_3_out, not_4_out, op, ovrfl, reg0WE, reg1WE,
       reg2WE, reg3WE, register_1_q, register_2_q, register_3_q, regWrite, store;
  wire [1:0] Rd, Rs;
  wire [3:0] register_4_q, register_4_q_2, register_5_q, register_5_q_2, register_6_q, register_6_q_2;
  wire [5:0] programcounter2_1_loc, trgt;
  wire [7:0] instr, ram_1_dout;
  wire [15:0] InB, multiplexer_1_out, multiplexer_2_out, multiplexer_4_out, multiplexer_5_out, myVal, outpt,
       ram_2_dout, srcsel_2_regout, srcsel_4_regout, sum, undriven_2;
  wire [15:2] undriven;

  Clock clock_1 (.out(clk));
  Register #(.width(1)) register_1 (.D(1'b1), .en(1'b1), .clk(clk), .Q(register_1_q), .clr(in_1));
  Hex_Digit_Display hex_digit_display_1 (.value(out_2[15:12]));  // open: dp
  Hex_Digit_Display hex_digit_display_2 (.value(out_5[15:12]));  // open: dp
  Register #(.width(1)) register_2 (.D(register_1_q), .en(1'b1), .clk(clk), .Q(register_2_q), .clr(in_1));
  Hex_Digit_Display hex_digit_display_3 (.value(out_2[11:8]));  // open: dp
  Hex_Digit_Display hex_digit_display_4 (.value(out_2[7:4]));  // open: dp
  Hex_Digit_Display hex_digit_display_5 (.value(out_5[11:8]));  // open: dp
  Hex_Digit_Display hex_digit_display_6 (.value(out_5[7:4]));  // open: dp
  Hex_Digit_Display hex_digit_display_7 (.value(out_2[3:0]));  // open: dp
  Hex_Digit_Display hex_digit_display_8 (.value(out_5[3:0]));  // open: dp
  srcSel srcsel_1 (.reg0(out_2), .reg1(out_3), .reg2(out_5), .reg3(out_6), .sel(Rs), .regOut(InB));
  regWe regwe_1 (
    .Rd(Rd), .regWrite(regWrite), .regWrite0(reg0WE), .regWrite1(reg1WE), .regWrite2(reg2WE),
    .regWrite3(reg3WE));
  not not_1 (not_1_out, jmp);
  srcSel srcsel_2 (.reg0(out_2), .reg1(out_3), .reg2(out_5), .reg3(out_6), .sel(Rd), .regOut(srcsel_2_regout));
  not not_2 (not_2_out, store);
  Hex_Digit_Display hex_digit_display_9 (.value(out_3[15:12]));  // open: dp
  Hex_Digit_Display hex_digit_display_10 (.value(out_6[15:12]));  // open: dp
  Register #(.width(1)) register_3 (.D(regWrite), .en(ovrfl), .clk(clk), .Q(register_3_q), .clr(in_1));
  srcSel srcsel_3 (.reg0(out_2), .reg1(out_3), .reg2(out_5), .reg3(out_6), .sel(Rs), .regOut(myVal));
  and and_1 (regWrite, register_2_q, not_1_out, not_2_out);
  Hex_Digit_Display hex_digit_display_11 (.value(out_3[11:8]));  // open: dp
  Hex_Digit_Display hex_digit_display_12 (.value(out_3[7:4]));  // open: dp
  Hex_Digit_Display hex_digit_display_13 (.value(out_6[11:8]));  // open: dp
  Hex_Digit_Display hex_digit_display_14 (.value(out_6[7:4]));  // open: dp
  Hex_Digit_Display hex_digit_display_15 (.value(out_3[3:0]));  // open: dp
  Hex_Digit_Display hex_digit_display_16 (.value(out_6[3:0]));  // open: dp
  LED led_1 (.in(register_3_q));
  CSA_Adder_Subtractor csa_adder_subtractor_1 (.a(srcsel_2_regout), .b(InB), .op(op), .s(sum), .overflow(ovrfl));
  not not_3 (not_3_out, store);
  srcSel srcsel_4 (.reg0(out_2), .reg1(out_3), .reg2(out_5), .reg3(out_6), .sel(Rd), .regOut(srcsel_4_regout));
  Register #(.width(16)) R0 (.D(outpt), .en(reg0WE), .clk(clk), .Q(out_2), .clr(in_1));
  Register #(.width(16)) R1 (.D(outpt), .en(reg1WE), .clk(clk), .Q(out_3), .clr(in_1));
  Register #(.width(16)) R2 (.D(outpt), .en(reg2WE), .clk(clk), .Q(out_5), .clr(in_1));
  Register #(.width(16)) R3 (.D(outpt), .en(reg3WE), .clk(clk), .Q(out_6), .clr(in_1));
  programCounter2 programcounter2_1 (.target(trgt), .jump(jmp), .clk(clk), .rst(in_1), .loc(programcounter2_1_loc));
  programCounter programcounter_1 (.in_1(clk), .in_2(in_1), .out_3(out_4));
  RAM #(.addrWidth(6), .asyncread("true"), .trigger("falling")) ram_1 (
    .addr(programcounter2_1_loc), .we(1'b0), .oe(1'b1), .clk(clk), .dout(ram_1_dout));  // open: din
  RAM #(.addrWidth(4), .asyncread("true"), .dataWidth(16), .trigger("falling")) ram_2 (
    .addr(InB[3:0]), .we(store), .oe(not_3_out), .clk(clk), .din(srcsel_4_regout), .dout(ram_2_dout));
  Multiplexer #(.width(16)) multiplexer_1 (.in0(ram_2_dout), .in1({undriven, Rs}), .out(multiplexer_1_out), .sel(ldi));
  Register register_4 (.D(ram_1_dout), .en(1'b1), .clk(clk), .Q({register_4_q_2, register_4_q}), .clr(in_1));
  Multiplexer #(.width(16)) multiplexer_2 (.in0(sum), .in1(InB), .out(multiplexer_2_out), .sel(move));
  Multiplexer #(.width(16)) multiplexer_3 (
    .in0(multiplexer_1_out), .in1(multiplexer_2_out), .out(outpt), .sel(not_4_out));
  not not_4 (not_4_out, instr[3]);
  Hex_Digit_Display hex_digit_display_17 (.value(register_4_q_2));  // open: dp
  Hex_Digit_Display hex_digit_display_18 (.value(register_4_q));  // open: dp
  Register register_5 (
    .D({register_4_q_2, register_4_q}), .en(1'b1), .clk(clk), .Q({register_5_q_2, register_5_q}), .clr(in_1));
  Hex_Digit_Display hex_digit_display_19 (.value(register_5_q_2));  // open: dp
  Hex_Digit_Display hex_digit_display_20 (.value(register_5_q));  // open: dp
  Register register_6 (
    .D({register_5_q_2, register_5_q}), .en(1'b1), .clk(clk), .Q({register_6_q_2, register_6_q}), .clr(in_1));
  Hex_Digit_Display hex_digit_display_21 (.value(register_6_q_2));  // open: dp
  IRPipeline irpipeline_1 (
    .IR({register_4_q_2, register_4_q}), .clk(clk), .rst(in_1), .instruction(instr), .op(op), .move(move),
    .Rs(Rs), .store(store), .Rd(Rd), .loadimmediate(ldi), .load(ld), .halt(halt), .jump(jmp), .target(trgt));
  Hex_Digit_Display hex_digit_display_22 (.value(register_6_q));  // open: dp
  Multiplexer #(.width(16)) multiplexer_4 (.in0(undriven_2), .out(multiplexer_4_out), .sel(ld));  // open: in1
  Multiplexer #(.width(16)) multiplexer_5 (
    .in0(multiplexer_4_out), .in1({{14{1'b0}}, Rs}), .out(multiplexer_5_out), .sel(ldi));

  // Other names for the same wires on the sheet: R0[15:0] = out_2; R1[15:0] = out_3; R2[15:0] = out_5;
  //   R3[15:0] = out_6; rst = in_1

  // Notes on the sheet:
  //   LA: 4c41
  //   SA: 5341
  //   C : 7b43
  //   S: 537D
  //   B3, 43, E2, 32, 82
  //   Instruction Register
endmodule

module programCounter3 (
  input  [5:0] target,
  input  jump,
  input  clk,
  input  jumpnegative,
  input  rst,
  output [5:0] loc
);

  wire or_1_out;
  wire [5:0] adder_1_out, multiplexer_1_out;

  or or_1 (or_1_out, jump, jumpnegative);
  Register #(.width(6)) register_1 (.D(multiplexer_1_out), .clk(clk), .Q(loc), .clr(rst));  // open: en
  Multiplexer #(.width(6)) multiplexer_1 (.in0(adder_1_out), .in1(target), .out(multiplexer_1_out), .sel(or_1_out));
  Adder #(.width(6)) adder_1 (.a(6'b000001), .b(loc), .out(adder_1_out));  // open: cin, cout
endmodule

module IRJumpimproved (
  input  [7:0] IR,
  input  clk,
  input  rst,
  output [7:0] instruction,
  output op,
  output move,
  output [1:0] Rs,
  output store,
  output [1:0] Rd,
  output loadimmediate,
  output load,
  output halt,
  output jump,
  output [5:0] target,
  output jumpnegative
);

  wire and_1_out, and_2_out, and_3_out, and_4_out, and_5_out, and_6_out, and_7_out, and_8_out, and_9_out,
       flag, nor_1_out, nor_2_out, not_1_out, not_2_out, not_3_out, not_4_out, not_5_out, not_6_out,
       not_7_out, not_8_out, not_9_out;

  Register #(.width(2)) register_1 (.D(IR[5:4]), .clk(clk), .Q(Rs), .clr(rst));  // open: en
  Register #(.width(2)) register_2 (.D(IR[7:6]), .clk(clk), .Q(Rd), .clr(rst));  // open: en
  Register register_3 (.D(IR), .en(clk), .clk(1'b1), .Q(instruction), .clr(rst));
  not not_1 (not_1_out, IR[0]);
  and and_1 (and_1_out, IR[0], IR[1], IR[2], IR[3]);
  nor nor_1 (nor_1_out, IR[0], IR[1]);
  not not_2 (not_2_out, IR[0]);
  not not_3 (not_3_out, IR[2]);
  and and_2 (and_2_out, IR[3], IR[2], IR[1], not_1_out);
  nor nor_2 (nor_2_out, not_2_out, IR[1]);
  and and_3 (and_3_out, IR[0], IR[1], not_4_out, not_5_out);
  not not_4 (not_4_out, IR[2]);
  not not_5 (not_5_out, IR[3]);
  not not_6 (not_6_out, IR[0]);
  and and_4 (and_4_out, not_6_out, IR[1], IR[2], not_7_out);
  not not_7 (not_7_out, IR[3]);
  and and_5 (and_5_out, IR[3], not_3_out, IR[1], IR[0]);
  D_Flip_Flop d_ff_1 (.D(and_2_out), .clk(clk), .Q(loadimmediate), .reset(rst));  // open: Qn, preset
  D_Flip_Flop d_ff_2 (.D(and_1_out), .clk(clk), .Q(load), .reset(rst));  // open: Qn, preset
  and and_6 (and_6_out, nor_1_out, flag);
  D_Flip_Flop d_ff_3 (.D(and_3_out), .clk(clk), .Q(op), .reset(rst));  // open: Qn, preset
  D_Flip_Flop d_ff_4 (.D(and_4_out), .clk(clk), .Q(move), .reset(rst));  // open: Qn, preset
  D_Flip_Flop d_ff_5 (.D(and_5_out), .clk(clk), .Q(store), .reset(rst));  // open: Qn, preset
  D_Flip_Flop d_ff_6 (.D(and_6_out), .clk(clk), .Q(jump), .reset(rst));  // open: Qn, preset
  D_Flip_Flop d_ff_7 (.D(and_7_out), .clk(clk), .Q(jumpnegative), .reset(rst));  // open: Qn, preset
  and and_7 (and_7_out, nor_2_out, flag);
  D_Flip_Flop d_ff_8 (.D(1'b1), .clk(clk), .Q(flag), .reset(rst));  // open: Qn, preset
  not not_8 (not_8_out, IR[0]);
  and and_8 (and_8_out, not_8_out, IR[1], IR[2], not_9_out);
  not not_9 (not_9_out, IR[3]);
  and and_9 (and_9_out, and_8_out, IR[4], IR[5], IR[6], IR[7]);
  D_Flip_Flop d_ff_9 (.D(and_9_out), .clk(clk), .Q(halt), .reset(rst));  // open: Qn, preset

  assign target = IR[7:2];

  // Other names for the same wires on the sheet: bit0 = IR[4]; bit1 = IR[5]; bit2 = IR[6]; bit3 = IR[7]
endmodule
